# Fritzing sketch Wiring (saved by Fritzing 0.9.3b)

parts:
  Raspberry_Pi_1 = Raspberry Pi 3 [part_number=RPI-3-V1.2]  # not connected
  Part1 = Adafruit DC+Stepper Motor HAT [part_number="Adafruit #2348"]
  Turret_Firing_Motor = DC Motor
  Turret_UP/DOWN_Motor = DC Motor
  Right_Drive_Motor = DC Motor
  Left_Drive_Motor = DC Motor
  Laser_Diode = LD
  Turret_Reset_Limit_Switch = SWITCH-MOMENTARY-2 [package=tactile-pth]

nets:
  N1: Part1.M2A, Left_Drive_Motor.pin_1
  N2: Part1.M2B, Left_Drive_Motor.pin_2
  N3: Part1.M1B, Right_Drive_Motor.pin_1
  N4: Part1.M1A, Right_Drive_Motor.pin_2
  N5: Part1.M4A, Turret_Firing_Motor.pin_1
  N6: Part1.M4B, Turret_Firing_Motor.pin_2
  N7: Part1.GND, Laser_Diode.cathode
  N8: Part1.M3B, Turret_UP/DOWN_Motor.pin_1
  N9: Part1.M3A, Turret_UP/DOWN_Motor.pin_2
  N10: Part1.PWM0, Laser_Diode.anode
  N11: Part1.3.3V, Turret_Reset_Limit_Switch.2
  N12: Part1.GPIO21, Turret_Reset_Limit_Switch.1

custom parts:
  Adafruit DC+Stepper Motor HAT: Let your robotic dreams come true with the new DC+Stepper Motor HAT from Adafruit. This Raspberry Pi add-on is perfect for any motion project as it can drive up to 4 DC or 2 Stepper motors with full PWM speed control. Since the Raspberry Pi does not have a lot of PWM pins, we use a fully-dedicated PWM driver chip onboard to both control motor direction and speed. This chip handles all the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
  LD: A Generic Red Dot Laser Diode Module (~5mW)
